// Logisim project main.circ as structural Verilog: 5 circuits, main circuit UAL_RegistreFile
module registre16 (
  input  [15:0] DATA_IN,
  input  CLK,
  output [15:0] DATA_OUT
);

  Register register_1 (.D(DATA_IN[7:0]), .Q(DATA_OUT[7:0]), .clk(CLK));  // open: en, clr
  Register register_2 (.D(DATA_IN[15:8]), .Q(DATA_OUT[15:8]), .clk(CLK));  // open: en, clr
endmodule

module registrefile (
  input  [15:0] Data_in,
  input  CLK,
  input  [3:0] A1,
  input  [3:0] in_4,
  input  [3:0] A2,
  output [15:0] RD1,
  output [15:0] RD2
);

  wire and_1_out, and_2_out, and_3_out, and_4_out, and_5_out, and_6_out, and_7_out, and_8_out, and_9_out,
       and_10_out, and_11_out, and_12_out, and_13_out, and_14_out, and_15_out, and_16_out, decoder_1_out0,
       decoder_1_out1, decoder_1_out2, decoder_1_out3, decoder_1_out4, decoder_1_out5, decoder_1_out6,
       decoder_1_out7, decoder_1_out8, decoder_1_out9, decoder_1_out10, decoder_1_out11, decoder_1_out12,
       decoder_1_out13, decoder_1_out14, decoder_1_out15;
  wire [15:0] registre16_1_data_out, registre16_2_data_out, registre16_3_data_out, registre16_4_data_out,
       registre16_5_data_out, registre16_6_data_out, registre16_7_data_out, registre16_8_data_out,
       registre16_9_data_out, registre16_10_data_out, registre16_11_data_out, registre16_12_data_out,
       registre16_13_data_out, registre16_14_data_out, registre16_15_data_out, registre16_16_data_out;

  Decoder #(.select(4)) decoder_1 (
    .out0(decoder_1_out0), .out1(decoder_1_out1), .out2(decoder_1_out2), .out3(decoder_1_out3),
    .out4(decoder_1_out4), .out5(decoder_1_out5), .out6(decoder_1_out6), .out7(decoder_1_out7),
    .out8(decoder_1_out8), .out9(decoder_1_out9), .out10(decoder_1_out10), .out11(decoder_1_out11),
    .out12(decoder_1_out12), .out13(decoder_1_out13), .out14(decoder_1_out14), .out15(decoder_1_out15),
    .sel(in_4));  // open: en
  and and_1 (and_1_out, decoder_1_out0, CLK);
  and and_2 (and_2_out, decoder_1_out1, CLK);
  and and_3 (and_3_out, decoder_1_out2, CLK);
  and and_4 (and_4_out, decoder_1_out3, CLK);
  and and_5 (and_5_out, decoder_1_out4, CLK);
  and and_6 (and_6_out, decoder_1_out5, CLK);
  and and_7 (and_7_out, decoder_1_out6, CLK);
  and and_8 (and_8_out, decoder_1_out7, CLK);
  and and_9 (and_9_out, decoder_1_out8, CLK);
  and and_10 (and_10_out, decoder_1_out9, CLK);
  and and_11 (and_11_out, decoder_1_out10, CLK);
  and and_12 (and_12_out, decoder_1_out11, CLK);
  and and_13 (and_13_out, decoder_1_out12, CLK);
  and and_14 (and_14_out, decoder_1_out13, CLK);
  and and_15 (and_15_out, decoder_1_out14, CLK);
  and and_16 (and_16_out, decoder_1_out15, CLK);
  registre16 registre16_1 (.DATA_IN(Data_in), .DATA_OUT(registre16_1_data_out), .CLK(and_1_out));
  registre16 registre16_2 (.DATA_IN(Data_in), .DATA_OUT(registre16_2_data_out), .CLK(and_2_out));
  registre16 registre16_3 (.DATA_IN(Data_in), .DATA_OUT(registre16_3_data_out), .CLK(and_3_out));
  registre16 registre16_4 (.DATA_IN(Data_in), .DATA_OUT(registre16_4_data_out), .CLK(and_4_out));
  registre16 registre16_5 (.DATA_IN(Data_in), .DATA_OUT(registre16_5_data_out), .CLK(and_5_out));
  registre16 registre16_6 (.DATA_IN(Data_in), .DATA_OUT(registre16_6_data_out), .CLK(and_6_out));
  registre16 registre16_7 (.DATA_IN(Data_in), .DATA_OUT(registre16_7_data_out), .CLK(and_7_out));
  registre16 registre16_8 (.DATA_IN(Data_in), .DATA_OUT(registre16_8_data_out), .CLK(and_8_out));
  registre16 registre16_9 (.DATA_IN(Data_in), .DATA_OUT(registre16_9_data_out), .CLK(and_9_out));
  registre16 registre16_10 (.DATA_IN(Data_in), .DATA_OUT(registre16_10_data_out), .CLK(and_10_out));
  registre16 registre16_11 (.DATA_IN(Data_in), .DATA_OUT(registre16_11_data_out), .CLK(and_11_out));
  registre16 registre16_12 (.DATA_IN(Data_in), .DATA_OUT(registre16_12_data_out), .CLK(and_12_out));
  registre16 registre16_13 (.DATA_IN(Data_in), .DATA_OUT(registre16_13_data_out), .CLK(and_13_out));
  registre16 registre16_14 (.DATA_IN(Data_in), .DATA_OUT(registre16_14_data_out), .CLK(and_14_out));
  registre16 registre16_15 (.DATA_IN(Data_in), .DATA_OUT(registre16_15_data_out), .CLK(and_15_out));
  registre16 registre16_16 (.DATA_IN(Data_in), .DATA_OUT(registre16_16_data_out), .CLK(and_16_out));
  Multiplexer #(.select(4), .width(16)) multiplexer_1 (
    .in0(registre16_1_data_out), .in1(registre16_2_data_out), .in2(registre16_3_data_out),
    .in3(registre16_4_data_out), .in4(registre16_5_data_out), .in5(registre16_6_data_out),
    .in6(registre16_7_data_out), .in7(registre16_8_data_out), .in8(registre16_9_data_out),
    .in9(registre16_10_data_out), .in10(registre16_11_data_out), .in11(registre16_12_data_out),
    .in12(registre16_13_data_out), .in13(registre16_14_data_out), .in14(registre16_15_data_out),
    .in15(registre16_16_data_out), .out(RD1), .sel(A1));  // open: en
  Multiplexer #(.select(4), .width(16)) multiplexer_2 (
    .in0(registre16_1_data_out), .in1(registre16_2_data_out), .in2(registre16_3_data_out),
    .in3(registre16_4_data_out), .in4(registre16_5_data_out), .in5(registre16_6_data_out),
    .in6(registre16_7_data_out), .in7(registre16_8_data_out), .in8(registre16_9_data_out),
    .in9(registre16_10_data_out), .in10(registre16_11_data_out), .in11(registre16_12_data_out),
    .in12(registre16_13_data_out), .in13(registre16_14_data_out), .in14(registre16_15_data_out),
    .in15(registre16_16_data_out), .out(RD2), .sel(A2));  // open: en
endmodule

module UAL_RegistreFile (
  input  in_1,
  input  in_2,
  input  in_3,
  input  in_4,
  input  in_5,
  input  [15:0] in_6,
  input  [15:0] in_7,
  input  [7:0] in_8,
  input  [3:0] in_9,
  output [15:0] OUtput,
  output [3:0] flags,
  output [15:0] out_12
);

  wire clk_ctrl, clock_1_out, multiplexer_3_out, not_1_out;
  wire [3:0] multiplexer_2_out;
  wire [7:0] adder_1_out, multiplexer_1_out, PC;
  wire [15:0] multiplexer_4_out, registrefile_1_rd1, registrefile_1_rd2;

  nor nor_1 (clk_ctrl, out_12[15], clock_1_out);
  Clock clock_1 (.out(clock_1_out));
  Multiplexer #(.width(8)) multiplexer_1 (.in0(PC), .in1(in_8), .out(multiplexer_1_out), .sel(in_5));  // open: en
  Register register_1 (.D(adder_1_out), .Q(PC), .clk(clk_ctrl), .clr(in_1));  // open: en
  not not_1 (not_1_out, in_5);
  assign out_12 = in_5 ? in_6 : 16'bz;  // Controlled_Buffer controlled_buffer_1
  RAM #(.dataWidth(16)) ram_1 (
    .addr(multiplexer_1_out), .data(out_12), .sel(1'b1), .clk(in_4), .ld(not_1_out), .clr(in_3));
  Adder adder_1 (.a(PC), .b(8'h1), .out(adder_1_out));  // open: cin, cout
  Multiplexer #(.width(4)) multiplexer_2 (
    .in0(out_12[11:8]), .in1(in_9), .out(multiplexer_2_out), .sel(in_5));  // open: en
  Multiplexer multiplexer_3 (.in0(clk_ctrl), .in1(in_2), .out(multiplexer_3_out), .sel(in_5));  // open: en
  Multiplexer #(.width(16)) multiplexer_4 (.in0(OUtput), .in1(in_7), .out(multiplexer_4_out), .sel(in_5));  // open: en
  registrefile registrefile_1 (
    .Data_in(multiplexer_4_out), .CLK(multiplexer_3_out), .in_4(multiplexer_2_out), .RD1(registrefile_1_rd1),
    .A1(out_12[7:4]), .RD2(registrefile_1_rd2), .A2(out_12[3:0]));
  UAL ual_1 (.OP(out_12[14:12]), .Result(OUtput), .A(registrefile_1_rd2), .B(registrefile_1_rd1), .OF_SF_ZF_CF(flags));

  // Other names for the same wires on the sheet: A_in[3:0] = in_9; active = in_5; D_in[15:0] = in_7;
  //   inst_adr[7:0] = in_8; Inst_in[15:0] = in_6; stop = out_12[15]

  // Notes on the sheet:
  //   memoire d'instructions
  //   Write Data
  //   active =1 pour remplir la memoire d'instruction et le registre File manuellement
  //   output inst_mem
  //   le registre File
  //   code instruction :
  //   OP | RD | RS1 | RS2
  //   OF,SF,ZF,CF
  //   0-16
  //   0-16
  //   OP : code Operation 
  //   000 == addition
  //   001 == soustraction
  //   010 == multiplication
  //   011 == division
  //   100 == ET logique 
  //   101 == OU logique
  //   110 == NOR
  //   111= inverseur
  //   RD : registre distination
  //   0000 - 1111
  //   RS1,RS2 : registre source
  //   0000 - 1111
endmodule

module UAL (
  input  [15:0] A,
  input  [15:0] B,
  input  [2:0] OP,
  output [15:0] Result,
  output [3:0] OF_SF_ZF_CF
);

  wire C_minus, C_plus, OF_minus, OF_plus, undriven, undriven_2;
  wire [15:0] adder_1_out, and_1_out, divider_1_out, multiplier_1_out, not_1_out, or_1_out, subtractor_1_out,
       xor_1_out;

  Adder #(.width(16)) adder_1 (.a(A), .b(B), .out(adder_1_out), .cout(C_plus));  // open: cin
  Subtractor #(.width(16)) subtractor_1 (.a(B), .b(A), .out(subtractor_1_out), .bout(C_minus));  // open: bin
  Multiplier #(.width(16)) multiplier_1 (.a(A), .b(B), .out(multiplier_1_out));  // open: cin, cout
  Divider #(.width(16)) divider_1 (.a(A), .b(B), .out(divider_1_out));  // open: upper, rem
  assign and_1_out = A & B;  // AND_Gate and_1, 16 bits wide
  assign or_1_out = A | B;  // OR_Gate or_1, 16 bits wide
  assign xor_1_out = A ^ B;  // XOR_Gate xor_1, 16 bits wide
  assign not_1_out = ~A;  // NOT_Gate not_1, 16 bits wide
  OF_flag of_flag_1 (
    .A(A), .B(B), .S({OF_SF_ZF_CF[2], Result[14:0]}), .in_5(OP), .OF_plus(OF_plus), .OF_minus(OF_minus),
    .OF(OF_SF_ZF_CF[3]));  // open: in_3
  Multiplexer #(.select(3), .width(16)) multiplexer_1 (
    .in0(adder_1_out), .in1(subtractor_1_out), .in2(multiplier_1_out), .in3(divider_1_out), .in4(and_1_out),
    .in5(or_1_out), .in6(xor_1_out), .in7(not_1_out), .out({OF_SF_ZF_CF[2], Result[14:0]}), .sel(OP),
    .en(undriven));
  nor nor_1 (OF_SF_ZF_CF[1], Result[0], Result[1], Result[2], Result[3], Result[4], Result[5], Result[6], Result[7], Result[8], Result[9], Result[10], Result[11], Result[12], Result[13], Result[14], OF_SF_ZF_CF[2]);
  Multiplexer #(.select(3)) multiplexer_2 (
    .in0(C_plus), .in1(C_minus), .in2(1'b0), .in3(1'b0), .in4(1'b0), .in5(1'b0), .in6(1'b0), .in7(1'b0),
    .out(OF_SF_ZF_CF[0]), .sel(OP), .en(undriven_2));

  assign Result[15] = OF_SF_ZF_CF[2];

  // Other names for the same wires on the sheet: CF = OF_SF_ZF_CF[0]; ZF = OF_SF_ZF_CF[1]; SF = OF_SF_ZF_CF[2];
  //   OF = OF_SF_ZF_CF[3]

  // Notes on the sheet:
  //   sinon CF=0
  //   si OP=000 alors CF=CF+
  //   si OP=001 alors CF=CF-
endmodule

module OF_flag (
  input  [15:0] A,
  input  [15:0] B,
  input  in_3,
  input  [15:0] S,
  input  [2:0] in_5,
  output OF_plus,
  output OF_minus,
  output OF
);

  wire and_1_out, and_2_out, and_3_out, and_4_out, not_1_out, not_2_out, not_3_out, not_4_out, not_5_out,
       not_6_out, undriven;

  not not_1 (not_1_out, S[15]);
  not not_2 (not_2_out, A[15]);
  not not_3 (not_3_out, B[15]);
  not not_4 (not_4_out, B[15]);
  not not_5 (not_5_out, S[15]);
  not not_6 (not_6_out, A[15]);
  and and_1 (and_1_out, A[15], B[15], not_1_out);
  and and_2 (and_2_out, not_2_out, not_3_out, S[15]);
  and and_3 (and_3_out, A[15], not_4_out, not_5_out);
  and and_4 (and_4_out, not_6_out, B[15], S[15]);
  or or_1 (OF_plus, and_1_out, and_2_out);
  or or_2 (OF_minus, and_3_out, and_4_out);
  Multiplexer #(.select(3)) multiplexer_1 (
    .in0(OF_plus), .in1(OF_minus), .in2(in_3), .in3(in_3), .in4(in_3), .in5(in_3), .in6(in_3), .in7(in_3),
    .out(OF), .sel(in_5), .en(undriven));

  // Notes on the sheet:
  //   Signe A
  //   Signe B
  //   Signe S
endmodule
